// Logisim project ex1_e.circ as structural Verilog: 1 circuit, main circuit main
module main (
  input  A1,
  input  A0,
  input  B1,
  input  B0,
  output Y0,
  output Y1,
  output Y2
);

  wire and_1_out, and_3_out, E0, E1, G0, G1, L0, L1;

  Comparator #(.width(1)) comparator_1 (.a(A1), .b(B1), .gt(G1), .eq(E1), .lt(L1));
  Comparator #(.width(1)) comparator_2 (.a(A0), .b(B0), .gt(G0), .eq(E0), .lt(L0));
  and and_1 (and_1_out, E1, G0);
  and and_2 (Y1, E1, E0);
  and and_3 (and_3_out, E1, L0);
  or or_1 (Y0, G1, and_1_out);
  or or_2 (Y2, L1, and_3_out);
endmodule
