// Logisim project ex3_d.circ as structural Verilog: 3 circuits, main circuit main
module main (
  input  INPUT0,
  output OUTPUT0
);

  wire clock_1_out;
  wire [2:0] register_1_q, transition_1_ns0;

  transition transition_1 (
    .CS2(register_1_q[2]), .CS1(register_1_q[1]), .CS0(register_1_q[0]), .INPUT(INPUT0),
    .NS2(transition_1_ns0[2]), .NS1(transition_1_ns0[1]), .NS0(transition_1_ns0[0]));
  Clock clock_1 (.out(clock_1_out));
  Register #(.width(3)) register_1 (.D(transition_1_ns0), .clk(clock_1_out), .Q(register_1_q));  // open: en, clr
  calc_out calc_out_1 (.CS1(register_1_q[1]), .CS0(register_1_q[0]), .CS2(register_1_q[2]), .OUTPUT(OUTPUT0));
endmodule

module transition (
  input  CS2,
  input  CS1,
  input  CS0,
  input  INPUT,
  output NS2,
  output NS1,
  output NS0
);

  wire and_1_out, not_1_out, not_2_out;

  not not_1 (not_1_out, CS2);
  not not_2 (not_2_out, INPUT);
  and and_1 (and_1_out, not_1_out, not_2_out);
  or or_1 (NS1, and_1_out, CS0);

  assign NS0 = INPUT;
  assign NS2 = 1'b1;
endmodule

module calc_out (
  input  CS1,
  input  CS0,
  input  CS2,
  output OUTPUT
);

  wire and_1_out, and_2_out, not_1_out, not_2_out;

  not not_1 (not_1_out, CS1);
  not not_2 (not_2_out, CS0);
  and and_1 (and_1_out, not_1_out, not_2_out, CS2);
  and and_2 (and_2_out, CS1, CS0);
  or or_1 (OUTPUT, and_1_out, and_2_out);
endmodule
