// Logisim project ex3.circ as structural Verilog: 1 circuit, main circuit Split
module Split (
  input  [7:0] IN1,
  output OUT1,
  output OUT2,
  output [8:0] OUT3,
  output [8:0] OUT4
);

  wire [3:0] bitadder_1_out;
  wire [7:0] adder_1_out, not_2_out;
  wire [8:0] bit_extender_1_out, bit_extender_2_out;

  not not_1 (OUT3[8], OUT1);
  xor xor_1 (OUT1, IN1[0], IN1[1], IN1[2], IN1[3], IN1[4], IN1[5], IN1[6], IN1[7]);
  assign not_2_out = ~IN1;  // NOT_Gate not_2, 8 bits wide
  assign bit_extender_1_out = {{1{1'b0}}, IN1};  // Bit_Extender bit_extender_1
  BitAdder #(.width(1)) bitadder_1 (
    .in0(IN1[0]), .in1(IN1[1]), .in2(IN1[2]), .in3(IN1[3]), .in4(IN1[4]), .in5(IN1[5]), .in6(IN1[6]),
    .in7(IN1[7]), .out(bitadder_1_out));
  Adder adder_1 (.a(not_2_out), .b(8'h1), .out(adder_1_out));  // open: cin, cout
  Comparator #(.mode("unsigned"), .width(4)) comparator_1 (.a(bitadder_1_out), .b(4'b0100), .gt(OUT2));  // open: eq, lt
  assign bit_extender_2_out = {{1{1'b1}}, adder_1_out};  // Bit_Extender bit_extender_2
  Multiplexer #(.width(9)) multiplexer_1 (.in0(bit_extender_1_out), .in1(bit_extender_2_out), .out(OUT4), .sel(OUT2));

  assign OUT3[7:0] = IN1;

  // Other names for the same wires on the sheet: IN1_0 = IN1[0]; IN1_1 = IN1[1]; IN1_2 = IN1[2]; IN1_3 = IN1[3];
  //   IN1_4 = IN1[4]; IN1_5 = IN1[5]; IN1_6 = IN1[6]; IN1_7 = IN1[7]

  // Notes on the sheet:
  //   PUT CIRCUITRY HERE
endmodule
