// Logisim project ex5_p2.circ as structural Verilog: 3 circuits, main circuit Running_LED
module Running_LED (
  input  [7:0] INITIAL_LED,
  input  RST,
  output [7:0] OUT_LED
);

  wire clock_1_out, count_1_res_out;
  wire [7:0] multiplexer_1_out, register_1_q, rot1_1_out_2;

  Clock clock_1 (.out(clock_1_out));
  LED led_1 (.in(OUT_LED[7]));
  Multiplexer #(.width(8)) multiplexer_1 (.in0(OUT_LED), .in1(INITIAL_LED), .out(multiplexer_1_out), .sel(RST));
  LED led_2 (.in(OUT_LED[6]));
  Register register_1 (.D(multiplexer_1_out), .clk(clock_1_out), .Q(register_1_q));  // open: en, clr
  LED led_3 (.in(OUT_LED[5]));
  LED led_4 (.in(OUT_LED[4]));
  rot1 rot1_1 (.in_1(register_1_q), .out_2(rot1_1_out_2));
  LED led_5 (.in(OUT_LED[3]));
  Multiplexer #(.width(8)) multiplexer_2 (.in0(rot1_1_out_2), .in1(register_1_q), .out(OUT_LED), .sel(count_1_res_out));
  LED led_6 (.in(OUT_LED[2]));
  count count_1 (.RESET_IN(RST), .RESET_VAL(8'h9), .TIMER_IN(clock_1_out), .RES_OUT(count_1_res_out));
  LED led_7 (.in(OUT_LED[1]));
  LED led_8 (.in(OUT_LED[0]));

  // Notes on the sheet:
  //   PUT CIRCUITS HERE
endmodule

module rot1 (
  input  [7:0] in_1,
  output [7:0] out_2
);


  assign out_2 = {in_1[0], in_1[7:1]};
endmodule

module count (
  input  RESET_IN,
  input  [7:0] RESET_VAL,
  input  TIMER_IN,
  output RES_OUT
);

  wire not_1_out;
  wire [7:0] adder_1_out, multiplexer_1_out, register_1_q;

  not not_1 (not_1_out, RESET_IN);
  Adder adder_1 (.a(8'h1), .b(register_1_q), .out(adder_1_out));  // open: cin, cout
  Register register_1 (.D(multiplexer_1_out), .clk(TIMER_IN), .Q(register_1_q));  // open: en, clr
  Multiplexer #(.width(8)) multiplexer_1 (.in0({8{1'b0}}), .in1(adder_1_out), .out(multiplexer_1_out), .sel(not_1_out));
  Comparator comparator_1 (.a(RESET_VAL), .b(register_1_q), .lt(RES_OUT));  // open: gt, eq
endmodule
