// Logisim project proj_2_1_top.circ as structural Verilog: 8 circuits, main circuit testbench
module TOP (
  input  clk,
  input  rst,
  input  [31:0] inst,
  output [31:0] inst_addr,
  output mem_wen,
  output [31:0] mem_din,
  output [31:0] mem_dout,
  output [31:0] mem_addr,
  output control_en,
  output [31:0] control_pc,
  output wb_en,
  output [4:0] wb_addr,
  output [31:0] wb_data
);

  wire branchcomp_1_br_eq, branchcomp_1_br_lt, controller_1_br_un, controller_1_full_word,
       controller_1_op1_src, controller_1_op2_src, controller_1_pc_sel, controller_1_re, controller_1_reg_en,
       not_1_out, or_1_out;
  wire [1:0] controller_1_wb_src;
  wire [2:0] controller_1_alu_ctrl;
  wire [31:0] adder_1_out, alu_1_alu_out, and_2_out, immgen_1_imm, multiplexer_1_out, multiplexer_2_out,
       multiplexer_7_out, multiplexer_8_out, multiplexer_11_out, PC_Register_q, regfile_1_x_rs1,
       regfile_1_x_rs2;

  Multiplexer #(.width(32)) multiplexer_1 (
    .in0(alu_1_alu_out), .in1({32{1'b0}}), .out(multiplexer_1_out), .sel(or_1_out));
  Multiplexer #(.width(32)) multiplexer_2 (
    .in0(adder_1_out), .in1(alu_1_alu_out), .out(multiplexer_2_out), .sel(controller_1_pc_sel));
  or or_1 (or_1_out, rst, not_1_out);
  not not_1 (not_1_out, controller_1_pc_sel);
  assign control_pc = multiplexer_1_out & 32'hfffffffe;  // AND_Gate and_1, 32 bits wide
  Multiplexer multiplexer_3 (.in0(controller_1_pc_sel), .in1(1'b0), .out(control_en), .sel(rst));
  Register #(.width(32)) PC_Register (.D(and_2_out), .clk(clk), .Q(PC_Register_q), .clr(rst));  // open: en
  assign and_2_out = 32'hfffffffe & multiplexer_2_out;  // AND_Gate and_2, 32 bits wide
  Adder #(.width(32)) adder_1 (.a(32'h4), .b(PC_Register_q), .out(adder_1_out));  // open: cin, cout
  assign inst_addr = PC_Register_q & 32'hfe;  // AND_Gate and_3, 32 bits wide
  Multiplexer #(.width(5)) multiplexer_4 (.in0(inst[11:7]), .in1({5{1'b0}}), .out(wb_addr), .sel(rst));
  Multiplexer #(.width(32)) multiplexer_5 (.in0(multiplexer_11_out), .in1({32{1'b0}}), .out(wb_data), .sel(rst));
  Controller controller_1 (
    .insn(inst), .br_eq(branchcomp_1_br_eq), .br_lt(branchcomp_1_br_lt), .ALU_ctrl(controller_1_alu_ctrl),
    .reg_en(controller_1_reg_en), .op1_src(controller_1_op1_src), .op2_src(controller_1_op2_src),
    .br_un(controller_1_br_un), .wb_src(controller_1_wb_src), .re(controller_1_re), .we(mem_wen),
    .full_word(controller_1_full_word), .pc_sel(controller_1_pc_sel));
  Multiplexer multiplexer_6 (.in0(controller_1_reg_en), .in1(1'b0), .out(wb_en), .sel(rst));
  RegFile regfile_1 (
    .x_rd(multiplexer_11_out), .rd(inst[11:7]), .rs1(inst[19:15]), .rs2(inst[24:20]), .clk(clk), .rst(rst),
    .reg_en(controller_1_reg_en), .x_rs1(regfile_1_x_rs1), .x_rs2(regfile_1_x_rs2));
  ImmGen immgen_1 (.insn(inst), .imm(immgen_1_imm));
  BranchComp branchcomp_1 (
    .rs1(regfile_1_x_rs1), .rs2(regfile_1_x_rs2), .br_un(controller_1_br_un), .br_eq(branchcomp_1_br_eq),
    .br_lt(branchcomp_1_br_lt));
  Multiplexer #(.width(32)) multiplexer_7 (
    .in0(regfile_1_x_rs1), .in1(PC_Register_q), .out(multiplexer_7_out), .sel(controller_1_op1_src));
  Multiplexer #(.width(32)) multiplexer_8 (
    .in0(regfile_1_x_rs2), .in1(immgen_1_imm), .out(multiplexer_8_out), .sel(controller_1_op2_src));
  Multiplexer #(.width(32)) multiplexer_9 (.in0(alu_1_alu_out), .in1({32{1'b0}}), .out(mem_addr), .sel(rst));
  Multiplexer #(.width(32)) multiplexer_10 (.in0(regfile_1_x_rs2), .in1({32{1'b0}}), .out(mem_din), .sel(rst));
  ALU alu_1 (
    .in1(multiplexer_7_out), .in2(multiplexer_8_out), .ALU_ctrl(controller_1_alu_ctrl),
    .ALU_out(alu_1_alu_out));
  DataMemory datamemory_1 (
    .clk(clk), .rst(rst), .addr(alu_1_alu_out), .d_in(regfile_1_x_rs2), .re(controller_1_re), .we(mem_wen),
    .full_word(controller_1_full_word), .d_out(mem_dout));
  Multiplexer #(.select(2), .width(32)) multiplexer_11 (
    .in0(mem_dout), .in1(alu_1_alu_out), .in2(adder_1_out), .out(multiplexer_11_out),
    .sel(controller_1_wb_src));  // open: in3

  // Notes on the sheet:
  //   DON'T TOUCH!
  //   Instruction Memory
endmodule

module testbench (
  input  rst,
  output [5:0] out_2,
  output out_3,
  output halt,
  output [31:0] out_5,
  output [31:0] mem_dout,
  output [31:0] mem_addr,
  output out_8,
  output [31:0] out_9,
  output out_10,
  output [4:0] out_11,
  output [31:0] out_12
);

  wire and_1_out, carry, clk, not_1_out, not_2_out, por_1_out, rst_t;
  wire [31:0] inst, inst_addr;

  not not_1 (not_1_out, inst[2]);
  not not_2 (not_2_out, inst[3]);
  POR por_1 (.out(por_1_out));
  // Probe on inst_addr
  TOP top_1 (
    .clk(clk), .rst(rst_t), .inst(inst), .inst_addr(inst_addr), .mem_wen(out_3), .mem_din(out_5),
    .mem_dout(mem_dout), .mem_addr(mem_addr), .control_en(out_8), .control_pc(out_9), .wb_en(out_10),
    .wb_addr(out_11), .wb_data(out_12));
  Clock clock_1 (.out(clk));
  or or_1 (rst_t, rst, por_1_out);
  and and_1 (and_1_out, inst[0], inst[1], not_1_out, not_2_out, inst[4], inst[5], inst[6]);
  or or_2 (halt, and_1_out, carry);
  Counter #(.max('h3f), .width(6)) counter_1 (
    .clr(rst_t), .up(1'b1), .count(1'b1), .clk(clk), .carry(carry), .Q(out_2));  // open: load, D
  // ROM #(.line("quad"), .misaligned("true")) rom_1: pin names not known; wires that end beside it: inst_addr[7:0], inst[7:0], inst[15:8], inst[23:16], inst[31:24]
  // Probe on inst

  // Other names for the same wires on the sheet: control_en = out_8; control_pc[31:0] = out_9; mem_din[31:0] = out_5;
  //   mem_wen = out_3; wb_addr[4:0] = out_11; wb_data[31:0] = out_12; wb_en = out_10

  // Notes on the sheet:
  //   DON'T TOUCH!
  //   contents of rom_1 (hex, n*v repeats v):
  //   37 1a 0 0 97 a 0 0 93 0 10 0 33 81 10 0 93 71 f1 f 13 d2 11 0 93 2 60 ff 33 d3 12 40 b3 a3 2 0 13 b4
  //   12 0 23 20 2a 0 23 12 3a 0 63 80 3 2 83 24 a 0 3 15 4a 0 ef 5 c0 0 63 8 c0 0 ef 9 40 1 13 6 50 1 67
  //   89 5 0 23 24 a 0 ef f8 df ff 23 24 1a 0 73 0 10
  //   you can write any instruction in
endmodule

module RegFile (
  input  [31:0] x_rd,
  input  [4:0] rd,
  input  [4:0] rs1,
  input  [4:0] rs2,
  input  clk,
  input  rst,
  input  reg_en,
  output [31:0] x_rs1,
  output [31:0] x_rs2
);

  wire decoder_1_out1, decoder_1_out2, decoder_1_out3, decoder_1_out4, decoder_1_out5, decoder_1_out6,
       decoder_1_out7, decoder_1_out8, decoder_1_out9, decoder_1_out10, decoder_1_out11, decoder_1_out12,
       decoder_1_out13, decoder_1_out14, decoder_1_out15, decoder_1_out16, decoder_1_out17, decoder_1_out18,
       decoder_1_out19, decoder_1_out20, decoder_1_out21, decoder_1_out22, decoder_1_out23, decoder_1_out24,
       decoder_1_out25, decoder_1_out26, decoder_1_out27, decoder_1_out28, decoder_1_out29, decoder_1_out30,
       decoder_1_out31;
  wire [31:0] x1_q, x2_q, x3_q, x4_q, x5_q, x6_q, x7_q, x8_q, x9_q, x10_q, x11_q, x12_q, x13_q, x14_q, x15_q,
       x16_q, x17_q, x18_q, x19_q, x20_q, x21_q, x22_q, x23_q, x24_q, x25_q, x26_q, x27_q, x28_q, x29_q,
       x30_q, x31_q;

  Decoder #(.select(5)) decoder_1 (
    .out1(decoder_1_out1), .out2(decoder_1_out2), .out3(decoder_1_out3), .out4(decoder_1_out4),
    .out5(decoder_1_out5), .out6(decoder_1_out6), .out7(decoder_1_out7), .out8(decoder_1_out8),
    .out9(decoder_1_out9), .out10(decoder_1_out10), .out11(decoder_1_out11), .out12(decoder_1_out12),
    .out13(decoder_1_out13), .out14(decoder_1_out14), .out15(decoder_1_out15), .out16(decoder_1_out16),
    .out17(decoder_1_out17), .out18(decoder_1_out18), .out19(decoder_1_out19), .out20(decoder_1_out20),
    .out21(decoder_1_out21), .out22(decoder_1_out22), .out23(decoder_1_out23), .out24(decoder_1_out24),
    .out25(decoder_1_out25), .out26(decoder_1_out26), .out27(decoder_1_out27), .out28(decoder_1_out28),
    .out29(decoder_1_out29), .out30(decoder_1_out30), .out31(decoder_1_out31), .sel(rd), .en(reg_en));  // open: out0
  Register #(.width(32)) x8 (.D(x_rd), .en(decoder_1_out8), .clk(clk), .Q(x8_q), .clr(rst));
  Register #(.width(32)) x16 (.D(x_rd), .en(decoder_1_out16), .clk(clk), .Q(x16_q), .clr(rst));
  Register #(.width(32)) x24 (.D(x_rd), .en(decoder_1_out24), .clk(clk), .Q(x24_q), .clr(rst));
  Register #(.width(32)) x1 (.D(x_rd), .en(decoder_1_out1), .clk(clk), .Q(x1_q), .clr(rst));
  Register #(.width(32)) x9 (.D(x_rd), .en(decoder_1_out9), .clk(clk), .Q(x9_q), .clr(rst));
  Register #(.width(32)) x17 (.D(x_rd), .en(decoder_1_out17), .clk(clk), .Q(x17_q), .clr(rst));
  Register #(.width(32)) x25 (.D(x_rd), .en(decoder_1_out25), .clk(clk), .Q(x25_q), .clr(rst));
  Register #(.width(32)) x2 (.D(x_rd), .en(decoder_1_out2), .clk(clk), .Q(x2_q), .clr(rst));
  Register #(.width(32)) x10 (.D(x_rd), .en(decoder_1_out10), .clk(clk), .Q(x10_q), .clr(rst));
  Register #(.width(32)) x18 (.D(x_rd), .en(decoder_1_out18), .clk(clk), .Q(x18_q), .clr(rst));
  Register #(.width(32)) x26 (.D(x_rd), .en(decoder_1_out26), .clk(clk), .Q(x26_q), .clr(rst));
  Register #(.width(32)) x3 (.D(x_rd), .en(decoder_1_out3), .clk(clk), .Q(x3_q), .clr(rst));
  Register #(.width(32)) x11 (.D(x_rd), .en(decoder_1_out11), .clk(clk), .Q(x11_q), .clr(rst));
  Register #(.width(32)) x19 (.D(x_rd), .en(decoder_1_out19), .clk(clk), .Q(x19_q), .clr(rst));
  Register #(.width(32)) x27 (.D(x_rd), .en(decoder_1_out27), .clk(clk), .Q(x27_q), .clr(rst));
  Register #(.width(32)) x4 (.D(x_rd), .en(decoder_1_out4), .clk(clk), .Q(x4_q), .clr(rst));
  Register #(.width(32)) x12 (.D(x_rd), .en(decoder_1_out12), .clk(clk), .Q(x12_q), .clr(rst));
  Register #(.width(32)) x20 (.D(x_rd), .en(decoder_1_out20), .clk(clk), .Q(x20_q), .clr(rst));
  Register #(.width(32)) x28 (.D(x_rd), .en(decoder_1_out28), .clk(clk), .Q(x28_q), .clr(rst));
  Register #(.width(32)) x5 (.D(x_rd), .en(decoder_1_out5), .clk(clk), .Q(x5_q), .clr(rst));
  Register #(.width(32)) x13 (.D(x_rd), .en(decoder_1_out13), .clk(clk), .Q(x13_q), .clr(rst));
  Register #(.width(32)) x21 (.D(x_rd), .en(decoder_1_out21), .clk(clk), .Q(x21_q), .clr(rst));
  Register #(.width(32)) x29 (.D(x_rd), .en(decoder_1_out29), .clk(clk), .Q(x29_q), .clr(rst));
  Register #(.width(32)) x6 (.D(x_rd), .en(decoder_1_out6), .clk(clk), .Q(x6_q), .clr(rst));
  Register #(.width(32)) x14 (.D(x_rd), .en(decoder_1_out14), .clk(clk), .Q(x14_q), .clr(rst));
  Register #(.width(32)) x22 (.D(x_rd), .en(decoder_1_out22), .clk(clk), .Q(x22_q), .clr(rst));
  Register #(.width(32)) x30 (.D(x_rd), .en(decoder_1_out30), .clk(clk), .Q(x30_q), .clr(rst));
  Register #(.width(32)) x7 (.D(x_rd), .en(decoder_1_out7), .clk(clk), .Q(x7_q), .clr(rst));
  Register #(.width(32)) x15 (.D(x_rd), .en(decoder_1_out15), .clk(clk), .Q(x15_q), .clr(rst));
  Register #(.width(32)) x23 (.D(x_rd), .en(decoder_1_out23), .clk(clk), .Q(x23_q), .clr(rst));
  Register #(.width(32)) x31 (.D(x_rd), .en(decoder_1_out31), .clk(clk), .Q(x31_q), .clr(rst));
  Multiplexer #(.select(5), .width(32)) multiplexer_1 (
    .in0({32{1'b0}}), .in1(x1_q), .in2(x2_q), .in3(x3_q), .in4(x4_q), .in5(x5_q), .in6(x6_q), .in7(x7_q),
    .in8(x8_q), .in9(x9_q), .in10(x10_q), .in11(x11_q), .in12(x12_q), .in13(x13_q), .in14(x14_q),
    .in15(x15_q), .in16(x16_q), .in17(x17_q), .in18(x18_q), .in19(x19_q), .in20(x20_q), .in21(x21_q),
    .in22(x22_q), .in23(x23_q), .in24(x24_q), .in25(x25_q), .in26(x26_q), .in27(x27_q), .in28(x28_q),
    .in29(x29_q), .in30(x30_q), .in31(x31_q), .out(x_rs1), .sel(rs1));
  Multiplexer #(.select(5), .width(32)) multiplexer_2 (
    .in0({32{1'b0}}), .in1(x1_q), .in2(x2_q), .in3(x3_q), .in4(x4_q), .in5(x5_q), .in6(x6_q), .in7(x7_q),
    .in8(x8_q), .in9(x9_q), .in10(x10_q), .in11(x11_q), .in12(x12_q), .in13(x13_q), .in14(x14_q),
    .in15(x15_q), .in16(x16_q), .in17(x17_q), .in18(x18_q), .in19(x19_q), .in20(x20_q), .in21(x21_q),
    .in22(x22_q), .in23(x23_q), .in24(x24_q), .in25(x25_q), .in26(x26_q), .in27(x27_q), .in28(x28_q),
    .in29(x29_q), .in30(x30_q), .in31(x31_q), .out(x_rs2), .sel(rs2));

  // Notes on the sheet:
  //   I/O
endmodule

module Controller (
  input  [31:0] insn,
  input  br_eq,
  input  br_lt,
  output [2:0] ALU_ctrl,
  output reg_en,
  output op1_src,
  output op2_src,
  output br_un,
  output [1:0] wb_src,
  output re,
  output we,
  output full_word,
  output pc_sel
);

  wire and_1_out, and_2_out, and_3_out, and_4_out, and_5_out, and_6_out, and_7_out, and_8_out, and_9_out,
       and_14_out, and_15_out, and_16_out, not_1_out, not_2_out, not_3_out, not_4_out, not_5_out, not_6_out,
       not_7_out;

  not not_1 (not_1_out, insn[6]);
  not not_2 (not_2_out, insn[5]);
  not not_3 (not_3_out, insn[4]);
  not not_4 (not_4_out, insn[2]);
  not not_5 (not_5_out, insn[14]);
  not not_6 (not_6_out, insn[13]);
  not not_7 (not_7_out, insn[12]);
  and and_1 (and_1_out, insn[4], not_4_out, not_5_out, insn[13]);
  and and_2 (and_2_out, not_2_out, insn[4], not_4_out, not_6_out, insn[12]);
  and and_3 (and_3_out, not_2_out, insn[4], not_4_out, insn[13]);
  and and_4 (and_4_out, insn[5], insn[4], not_4_out, insn[12]);
  and and_5 (and_5_out, insn[5], not_4_out);
  and and_6 (and_6_out, not_2_out, insn[2]);
  and and_7 (and_7_out, not_4_out, not_5_out, not_6_out);
  or or_1 (reg_en, not_2_out, insn[4], insn[2]);
  and and_8 (and_8_out, not_2_out, insn[2]);
  and and_9 (and_9_out, not_3_out, not_4_out, not_6_out, not_7_out);
  or or_2 (op2_src, not_2_out, not_3_out, insn[2]);
  and and_10 (re, not_2_out, not_3_out);
  and and_11 (we, not_1_out, insn[5], not_3_out);
  and and_12 (wb_src[1], not_3_out, insn[2]);
  and and_13 (full_word, not_1_out, not_3_out, not_7_out);
  and and_14 (and_14_out, not_3_out, insn[2]);
  and and_15 (and_15_out, not_3_out, not_4_out, not_6_out, not_7_out);
  or or_3 (ALU_ctrl[2], and_1_out, and_2_out);
  or or_4 (ALU_ctrl[1], and_3_out, and_4_out);
  or or_5 (ALU_ctrl[0], and_5_out, and_6_out, not_3_out, and_7_out);
  or or_6 (op1_src, and_8_out, insn[3], and_9_out);
  and and_16 (and_16_out, and_15_out, br_eq);
  or or_7 (pc_sel, and_14_out, and_16_out);

  assign br_un = 1'b0;
  assign wb_src[0] = insn[4];

  // Notes on the sheet:
  //   I/O
endmodule

module ALU (
  input  [31:0] in1,
  input  [31:0] in2,
  input  [2:0] ALU_ctrl,
  output [31:0] ALU_out
);

  wire comparator_1_lt, comparator_2_lt;
  wire [31:0] adder_1_out, and_1_out, bit_extender_1_out, bit_extender_2_out, shifter_1_out, shifter_2_out;

  Adder #(.width(32)) adder_1 (.a(in1), .b(in2), .out(adder_1_out));  // open: cin, cout
  assign and_1_out = in1 & in2;  // AND_Gate and_1, 32 bits wide
  Shifter #(.shift("ar"), .width(32)) shifter_1 (.in(in1), .\dist (in2[4:0]), .out(shifter_1_out));
  Shifter #(.shift("lr"), .width(32)) shifter_2 (.in(in1), .\dist (in2[4:0]), .out(shifter_2_out));
  Comparator #(.width(32)) comparator_1 (.a(in1), .b(in2), .lt(comparator_1_lt));  // open: gt, eq
  Comparator #(.mode("unsigned"), .width(32)) comparator_2 (.a(in1), .b(in2), .lt(comparator_2_lt));  // open: gt, eq
  assign bit_extender_1_out = {{31{1'b0}}, comparator_1_lt};  // Bit_Extender bit_extender_1
  assign bit_extender_2_out = {{31{1'b0}}, comparator_2_lt};  // Bit_Extender bit_extender_2
  Multiplexer #(.select(3), .width(32)) multiplexer_1 (
    .in0(in2), .in1(adder_1_out), .in2(and_1_out), .in3(shifter_1_out), .in4(shifter_2_out),
    .in5(bit_extender_1_out), .in6(bit_extender_2_out), .in7({32{1'b0}}), .out(ALU_out), .sel(ALU_ctrl));

  // Notes on the sheet:
  //   I/O
endmodule

module DataMemory (
  input  clk,
  input  rst,
  input  [31:0] addr,
  input  [31:0] d_in,
  input  re,
  input  we,
  input  full_word,
  output [31:0] d_out
);

  wire and_1_out, and_2_out, and_3_out, and_4_out, mod0, mod1, mod2, mod3, not_1_out, not_2_out, not_3_out,
       not_4_out, not_5_out, not_6_out, or_1_out, or_2_out, or_3_out, or_4_out, re0, re1, re2, re3, we0, we1,
       we2, we3;
  wire [1:0] controlled_buffer_1_out, controlled_buffer_3_out, controlled_buffer_5_out,
       controlled_buffer_7_out;
  wire [7:0] addr_mod_0_dout, addr_mod_1_dout, addr_mod_2_dout, addr_mod_3_dout, d_in0, d_in1, d_in2, d_in3,
       d_out0, d_out1, d_out2, d_out3, multiplexer_6_out, multiplexer_8_out, multiplexer_9_out,
       multiplexer_10_out;
  wire [13:0] addr0, addr1, addr2, addr3;
  wire [15:0] adder_1_out, adder_2_out, adder_3_out, adder_4_out;
  wire [31:0] bit_extender_1_out;

  not not_1 (not_1_out, mod0);
  assign {addr0, controlled_buffer_1_out} = mod0 ? addr[15:0] : 16'bz;  // Controlled_Buffer controlled_buffer_1
  assign {addr0, controlled_buffer_1_out} = not_1_out ? adder_4_out : 16'bz;  // Controlled_Buffer controlled_buffer_2
  Decoder #(.select(2)) decoder_1 (.out0(mod0), .out1(mod1), .out2(mod2), .out3(mod3), .sel(addr[1:0]));  // open: en
  // Probe on d_in0
  Multiplexer #(.select(2), .width(8)) multiplexer_1 (
    .in0(d_in[7:0]), .in1(d_in[31:24]), .in2(d_in[23:16]), .in3(d_in[15:8]), .out(d_in0), .sel(addr[1:0]));
  not not_2 (not_2_out, addr[1]);
  not not_3 (not_3_out, addr[0]);
  // Probe on addr0
  RAM #(.addrWidth(14), .asyncread("true"), .clearpin("true")) addr_mod_0 (
    .addr(addr0), .we(we0), .oe(re0), .clk(clk), .din(d_in0), .dout(addr_mod_0_dout), .clr(rst));
  not not_4 (not_4_out, mod1);
  assign {addr1, controlled_buffer_3_out} = not_4_out ? adder_1_out : 16'bz;  // Controlled_Buffer controlled_buffer_3
  Adder #(.width(16)) adder_1 (.a({addr0, controlled_buffer_1_out}), .b(16'h1), .out(adder_1_out));  // open: cin, cout
  Multiplexer #(.select(2), .width(8)) multiplexer_2 (
    .in0(d_in[15:8]), .in1(d_in[7:0]), .in2(d_in[31:24]), .in3(d_in[23:16]), .out(d_in1), .sel(addr[1:0]));
  assign {addr1, controlled_buffer_3_out} = mod1 ? addr[15:0] : 16'bz;  // Controlled_Buffer controlled_buffer_4
  and and_1 (and_1_out, not_2_out, not_3_out);
  and and_2 (and_2_out, addr[1], addr[0]);
  or or_1 (or_1_out, not_2_out, full_word);
  and and_3 (and_3_out, not_2_out, addr[0]);
  and and_4 (and_4_out, addr[1], not_3_out);
  or or_2 (or_2_out, addr[1], full_word);
  or or_3 (or_3_out, and_1_out, and_2_out, full_word);
  or or_4 (or_4_out, and_3_out, and_4_out, full_word);
  Multiplexer #(.select(2), .width(8)) multiplexer_3 (
    .in0(d_in[23:16]), .in1(d_in[15:8]), .in2(d_in[7:0]), .in3(d_in[31:24]), .out(d_in2), .sel(addr[1:0]));
  not not_5 (not_5_out, mod2);
  assign {addr2, controlled_buffer_5_out} = not_5_out ? adder_2_out : 16'bz;  // Controlled_Buffer controlled_buffer_5
  Adder #(.width(16)) adder_2 (.a({addr1, controlled_buffer_3_out}), .b(16'h1), .out(adder_2_out));  // open: cin, cout
  and and_5 (re0, re, or_3_out);
  and and_6 (we0, we, or_3_out);
  and and_7 (re1, re, or_1_out);
  and and_8 (we1, we, or_1_out);
  and and_9 (re2, re, or_4_out);
  and and_10 (we2, we, or_4_out);
  and and_11 (re3, re, or_2_out);
  and and_12 (we3, we, or_2_out);
  Multiplexer #(.width(8)) multiplexer_4 (.in0({8{1'b0}}), .in1(addr_mod_0_dout), .out(d_out0), .sel(re0));
  assign {addr2, controlled_buffer_5_out} = mod2 ? addr[15:0] : 16'bz;  // Controlled_Buffer controlled_buffer_6
  Multiplexer #(.select(2), .width(8)) multiplexer_5 (
    .in0(d_in[31:24]), .in1(d_in[23:16]), .in2(d_in[15:8]), .in3(d_in[7:0]), .out(d_in3), .sel(addr[1:0]));
  not not_6 (not_6_out, mod3);
  assign {addr3, controlled_buffer_7_out} = not_6_out ? adder_3_out : 16'bz;  // Controlled_Buffer controlled_buffer_7
  Adder #(.width(16)) adder_3 (.a({addr2, controlled_buffer_5_out}), .b(16'h1), .out(adder_3_out));  // open: cin, cout
  // Probe on addr1
  RAM #(.addrWidth(14), .asyncread("true"), .clearpin("true")) addr_mod_1 (
    .addr(addr1), .we(we1), .oe(re1), .clk(clk), .din(d_in1), .dout(addr_mod_1_dout), .clr(rst));
  // Probe on d_in1
  assign {addr3, controlled_buffer_7_out} = mod3 ? addr[15:0] : 16'bz;  // Controlled_Buffer controlled_buffer_8
  Adder #(.width(16)) adder_4 (.a({addr3, controlled_buffer_7_out}), .b(16'h1), .out(adder_4_out));  // open: cin, cout
  Multiplexer #(.select(2), .width(8)) multiplexer_6 (
    .in0(d_out3), .in1(d_out0), .in2(d_out1), .in3(d_out2), .out(multiplexer_6_out), .sel(addr[1:0]));
  Multiplexer #(.width(8)) multiplexer_7 (.in0({8{1'b0}}), .in1(addr_mod_1_dout), .out(d_out1), .sel(re1));
  Multiplexer #(.select(2), .width(8)) multiplexer_8 (
    .in0(d_out2), .in1(d_out3), .in2(d_out0), .in3(d_out1), .out(multiplexer_8_out), .sel(addr[1:0]));
  // Probe on addr2
  RAM #(.addrWidth(14), .asyncread("true"), .clearpin("true")) addr_mod_2 (
    .addr(addr2), .we(we2), .oe(re2), .clk(clk), .din(d_in2), .dout(addr_mod_2_dout), .clr(rst));
  // Probe on d_in2
  Multiplexer #(.select(2), .width(8)) multiplexer_9 (
    .in0(d_out1), .in1(d_out2), .in2(d_out3), .in3(d_out0), .out(multiplexer_9_out), .sel(addr[1:0]));
  Multiplexer #(.select(2), .width(8)) multiplexer_10 (
    .in0(d_out0), .in1(d_out1), .in2(d_out2), .in3(d_out3), .out(multiplexer_10_out), .sel(addr[1:0]));
  Multiplexer #(.width(8)) multiplexer_11 (.in0({8{1'b0}}), .in1(addr_mod_2_dout), .out(d_out2), .sel(re2));
  assign bit_extender_1_out = {{16{multiplexer_9_out[7]}}, {multiplexer_9_out, multiplexer_10_out}};  // Bit_Extender bit_extender_1
  Multiplexer #(.width(32)) multiplexer_12 (
    .in0(bit_extender_1_out),
    .in1({multiplexer_6_out, multiplexer_8_out, multiplexer_9_out, multiplexer_10_out}), .out(d_out),
    .sel(full_word));
  // Probe on d_out
  // Probe on addr3
  RAM #(.addrWidth(14), .asyncread("true"), .clearpin("true")) addr_mod_3 (
    .addr(addr3), .we(we3), .oe(re3), .clk(clk), .din(d_in3), .dout(addr_mod_3_dout), .clr(rst));
  // Probe on d_in3
  Multiplexer #(.width(8)) multiplexer_13 (.in0({8{1'b0}}), .in1(addr_mod_3_dout), .out(d_out3), .sel(re3));

  // Other names for the same wires on the sheet: addr16[15:0] = addr[15:0]; addr_l2[1:0] = addr[1:0]

  // Notes on the sheet:
  //   I/O
endmodule

module ImmGen (
  input  [31:0] insn,
  output [31:0] imm
);

  wire and_2_out, and_3_out, and_4_out, not_1_out, not_2_out, not_3_out, not_4_out, not_5_out, not_6_out,
       not_7_out, not_8_out, signed_12, signed_12_save, signed_13, unsigned_5, unsigned_20;
  wire [31:0] bit_extender_1_out, bit_extender_2_out, bit_extender_3_out, bit_extender_4_out,
       bit_extender_5_out;

  not not_1 (not_1_out, insn[6]);
  not not_2 (not_2_out, insn[5]);
  not not_3 (not_3_out, insn[4]);
  not not_4 (not_4_out, insn[3]);
  not not_5 (not_5_out, insn[2]);
  not not_6 (not_6_out, insn[14]);
  not not_7 (not_7_out, insn[13]);
  not not_8 (not_8_out, insn[12]);
  and and_1 (unsigned_5, not_2_out, insn[4], not_5_out, not_7_out, insn[12]);
  and and_2 (and_2_out, not_2_out, not_5_out, not_6_out);
  and and_3 (and_3_out, not_2_out, not_5_out, insn[13]);
  and and_4 (and_4_out, not_3_out, not_4_out, insn[2]);
  and and_5 (unsigned_20, insn[4], insn[2]);
  and and_6 (signed_13, not_3_out, not_5_out, not_7_out, not_8_out);
  and and_7 (signed_12_save, not_1_out, insn[5], not_3_out);
  or or_1 (signed_12, and_2_out, and_3_out, and_4_out);
  assign bit_extender_1_out = {{27{1'b0}}, insn[24:20]};  // Bit_Extender bit_extender_1
  assign bit_extender_2_out = {{20{insn[31]}}, insn[31:20]};  // Bit_Extender bit_extender_2
  assign bit_extender_3_out = {{20{insn[31]}}, {insn[31:25], insn[11:7]}};  // Bit_Extender bit_extender_3
  assign imm = unsigned_5 ? bit_extender_1_out : 32'bz;  // Controlled_Buffer controlled_buffer_1
  assign imm = signed_12 ? bit_extender_2_out : 32'bz;  // Controlled_Buffer controlled_buffer_2
  assign imm = unsigned_20 ? {insn[31:12], {12{1'b0}}} : 32'bz;  // Controlled_Buffer controlled_buffer_3
  assign bit_extender_4_out = {{11{insn[31]}}, {insn[31], insn[19:12], insn[20], insn[30:21], 1'b0}};  // Bit_Extender bit_extender_4
  assign bit_extender_5_out = {{19{insn[31]}}, {insn[31], insn[7], insn[30:25], insn[11:8], 1'b0}};  // Bit_Extender bit_extender_5
  assign imm = signed_12_save ? bit_extender_3_out : 32'bz;  // Controlled_Buffer controlled_buffer_4
  assign imm = insn[3] ? bit_extender_4_out : 32'bz;  // Controlled_Buffer controlled_buffer_5
  assign imm = signed_13 ? bit_extender_5_out : 32'bz;  // Controlled_Buffer controlled_buffer_6

  // Other names for the same wires on the sheet: signed_21 = insn[3]

  // Notes on the sheet:
  //   I/O
endmodule

module BranchComp (
  input  [31:0] rs1,
  input  [31:0] rs2,
  input  br_un,
  output br_eq,
  output br_lt
);

  wire comparator_1_eq, comparator_1_lt, comparator_2_eq, comparator_2_lt;

  Comparator #(.width(32)) comparator_1 (.a(rs1), .b(rs2), .eq(comparator_1_eq), .lt(comparator_1_lt));  // open: gt
  Comparator #(.mode("unsigned"), .width(32)) comparator_2 (
    .a(rs1), .b(rs2), .eq(comparator_2_eq), .lt(comparator_2_lt));  // open: gt
  Multiplexer multiplexer_1 (.in0(comparator_1_eq), .in1(comparator_2_eq), .out(br_eq), .sel(br_un));
  Multiplexer multiplexer_2 (.in0(comparator_1_lt), .in1(comparator_2_lt), .out(br_lt), .sel(br_un));

  // Notes on the sheet:
  //   I/O
endmodule
